# Fritzing sketch GrowBox-1.0 (saved by Fritzing 0.7.12b)
breadboards: 1

parts:
  R4 = Resistor [resistance=10k tolerance=±5% package=THT]
  R5 = Photocell (LDR) [package=THT]
  Arduino1 = Arduino
  M1 = DC Motor
  Q1 = Basic FET P-Channel [package="TO220 [THT]"]
  R6 = Resistor [tolerance=±5% resistance=220 package=THT]
  RHT1 = Humidity and Temperature Sensor RHT03
  S1 = Toggle Switch [package=THT]
  R7 = Rotary Potentiometer (Small) [maximum_resistance=100kΩ]

nets (from the breadboard view):
  +5V: R4.Pin_0, R5.pin_1, Arduino1.+5V, RHT1.Vcc, R7.leg2
  N1: R4.Pin_1, R5.pin_0, Arduino1.A0
  N2: Arduino1.GND, Q1.source, RHT1.GND_1, R7.leg1
  N3: Arduino1.D5, RHT1.Data-signal
  N4: Arduino1.D2, S1.L1
  N5: Arduino1.VIN, M1.pin_2
  N6: Arduino1.A2, R7.wiper
  N7: M1.pin_1, Q1.drain
  N8: Q1.gate, R6.Pin_1
