# Fritzing sketch GrowBox-1.1 (saved by Fritzing 0.7.12b)
breadboards: 1

parts:
  Q1 = TIP120 Hi-Current Darlington Transistor
  M1 = DC Motor
  R1 = Resistor [tolerance=±5% resistance=2.2k package=THT]
  Part1 = Humidity Sensor - HIH-4030 Breakout
  Arduino1 = Arduino
  DHT1 = DHT11 Humitidy and Temperature Sensor  # not connected
  D1 = Rectifier Diode [part_number=1N4001 package="Melf DO-213 AB [SMD]"]

nets:
  N1: Q1.BASE, R1.Pin_1
  N2: Q1.COLLECTOR, M1.pin_1, D1.anode
  GND: Q1.EMITTER, Part1.GND, Arduino1.GND
  N3: M1.pin_2, Arduino1.VIN, D1.cathode
  N4: R1.Pin_0, Arduino1.D3
  N5: Part1.OUT, Arduino1.A2
  VCC: Part1.VCC, Arduino1.+5V

custom parts:
  DHT11 Humitidy and Temperature Sensor: DHT11 Humidity and Temperature Sensor
